// Logisim project Lab 2.circ as structural Verilog
module Subtract_32bit (
);

  wire subtractor_1_bout, subtractor_2_bout, subtractor_3_bout, subtractor_4_bout, undriven_6, undriven_10;
  wire [7:0] subtractor_1_out, subtractor_2_out, subtractor_3_out, subtractor_4_out, undriven, undriven_2,
       undriven_3, undriven_4, undriven_5, undriven_7, undriven_8, undriven_9;

  Subtractor subtractor_1 (
    .a(undriven_8), .b(undriven_3), .out(subtractor_1_out), .bin(undriven_6), .bout(subtractor_1_bout));
  Subtractor subtractor_2 (
    .a(undriven_2), .b(undriven_9), .out(subtractor_2_out), .bin(subtractor_1_bout), .bout(subtractor_2_bout));
  Subtractor subtractor_3 (
    .a(undriven), .b(undriven_5), .out(subtractor_3_out), .bin(undriven_10), .bout(subtractor_3_bout));
  Subtractor subtractor_4 (
    .a(undriven_7), .b(undriven_4), .out(subtractor_4_out), .bin(subtractor_3_bout), .bout(subtractor_4_bout));

  // Notes on the sheet:
  //   X[31]
  //   X[30]
  //   .
  //   .
  //   .
  //   .
  //   X[01]
  //   X[00]
  //   Y[31]
  //   Y[30]
  //   .
  //   .
  //   .
  //   .
  //   Y[01]
  //   Y[00]
  //   C_IN
  //   32 Bit Ripple Subtractor
  //   .
  //   .
  //   .
  //   .
  //   C_OUT
  //   Z[31]
  //   Z[30]
  //   .
  //   .
  //   .
  //   .
  //   Z[01]
  //   Z[00]
endmodule

module Add_32_Bit (
);

  wire adder_1_cout, adder_1_out, adder_2_cout, adder_2_out, adder_3_cout, adder_3_out, adder_4_cout,
       adder_4_out, undriven, undriven_2, undriven_3, undriven_4, undriven_5, undriven_6, undriven_7,
       undriven_8, undriven_9, undriven_10;

  Adder #(.width(1)) adder_1 (.a(undriven), .b(undriven_9), .out(adder_1_out), .cin(adder_2_cout), .cout(adder_1_cout));
  Adder #(.width(1)) adder_2 (
    .a(undriven_2), .b(undriven_5), .out(adder_2_out), .cin(undriven_10), .cout(adder_2_cout));
  Adder #(.width(1)) adder_3 (
    .a(undriven_3), .b(undriven_6), .out(adder_3_out), .cin(adder_4_cout), .cout(adder_3_cout));
  Adder #(.width(1)) adder_4 (.a(undriven_4), .b(undriven_7), .out(adder_4_out), .cin(undriven_8), .cout(adder_4_cout));

  // Notes on the sheet:
  //   X[31]
  //   X[30]
  //   .
  //   .
  //   .
  //   .
  //   X[01]
  //   X[00]
  //   Y[31]
  //   Y[30]
  //   .
  //   .
  //   .
  //   .
  //   Y[01]
  //   Y[00]
  //   C_IN
  //   32 Bit Ripple Adder
  //   .
  //   .
  //   .
  //   .
  //   C_OUT
  //   Z[31]
  //   Z[30]
  //   .
  //   .
  //   .
  //   .
  //   Z[01]
  //   Z[00]
endmodule

module Add_1_Bit (
);

  wire and_1_out, multiplexer_1_out, or_1_out, undriven, undriven_2, undriven_3, xor_1_out, xor_2_out;

  xor xor_1 (xor_1_out, undriven_3, undriven);
  and and_1 (and_1_out, undriven, undriven_2);
  or or_1 (or_1_out, undriven, undriven_2);
  xor xor_2 (xor_2_out, xor_1_out, undriven_2);
  Multiplexer #(.enable("false")) multiplexer_1 (
    .in0(and_1_out), .in1(or_1_out), .out(multiplexer_1_out), .sel(undriven_3));

  // Notes on the sheet:
  //   X
  //   Y
  //   C_IN
  //   1 Bit Adder
  //   Z
  //   C_OUT
endmodule

module Subtract_1_Bit (
);

  wire and_1_out, multiplexer_1_out, or_1_out, undriven, undriven_2, undriven_3, xor_1_out, xor_2_out;

  xor xor_1 (xor_1_out, undriven_3, undriven);
  or or_1 (or_1_out, undriven, undriven_2);
  and and_1 (and_1_out, undriven, undriven_2);
  xor xor_2 (xor_2_out, xor_1_out, undriven_2);
  Multiplexer #(.enable("false")) multiplexer_1 (
    .in0(or_1_out), .in1(and_1_out), .out(multiplexer_1_out), .sel(undriven_3));

  // Notes on the sheet:
  //   X
  //   Y
  //   C_IN
  //   1 Bit Subtracter
  //   Z
  //   C_OUT
endmodule

module Shift_Left_1_Bit (
);

  wire multiplexer_1_out, undriven, undriven_2, undriven_4, undriven_5, undriven_6, undriven_7;
  wire [4:0] undriven_3;

  Subtract_32bit subtract_32bit_1 ();
  Set_Less_Than set_less_than_1 ();
  Multiplexer #(.select(5), .enable("false")) multiplexer_1 (
    .in0(undriven_2), .in1(undriven_4), .in30(undriven_5), .in31(undriven), .out(multiplexer_1_out),
    .sel(undriven_3));  // open: in2, in3, in4, in5, in6, in7, in8, in9, in10, in11, in12, in13, in14, in15, in16, in17, in18, in19, in20, in21, in22, in23, in24, in25, in26, in27, in28, in29
  Multiplexer #(.enable("false")) multiplexer_2 (
    .in0(multiplexer_1_out), .in1(undriven_7), .sel(undriven_6));  // open: out

  // Notes on the sheet:
  //   X[31]
  //   X[30]
  //   .
  //   .
  //   .
  //   .
  //   X[01]
  //   X[00]
  //   Y[31]
  //   Y[30]
  //   .
  //   .
  //   .
  //   .
  //   Y[01]
  //   Y[00]
  //   I[31]
  //   I30]
  //   .
  //   .
  //   .
  //   .
  //   I[01]
  //   I[00]
  //   1'b0
  //   32'd0
  //   Z
endmodule

module Set_Less_Than (
);

  wire multiplexer_1_out, undriven, undriven_2, undriven_3, xor_1_out;

  Subtract_32bit subtract_32bit_1 ();
  xor xor_1 (xor_1_out, undriven, undriven_2);
  Multiplexer #(.enable("false")) multiplexer_1 (
    .in0(undriven_3), .in1(undriven), .out(multiplexer_1_out), .sel(xor_1_out));

  // Notes on the sheet:
  //   X[31]
  //   X[30]
  //   .
  //   .
  //   .
  //   .
  //   X[01]
  //   X[00]
  //   Y[31]
  //   Y[30]
  //   .
  //   .
  //   .
  //   .
  //   Y[01]
  //   Y[00]
  //   1'b0
  //   S[31]
  //   S[30]
  //   .
  //   .
  //   .
  //   .
  //   S[01]
  //   S[00]
  //   Z
endmodule

module Equals (
);

  wire and_1_out, undriven, undriven_2, xnor_1_out;

  xnor xnor_1 (xnor_1_out, undriven, undriven_2);
  and and_1 (and_1_out, xnor_1_out, xnor_1_out);

  // Notes on the sheet:
  //   X[31:0]
  //   Y[31:0]
  //   Z
endmodule

module Shift_Right_1_Bit (
);

  wire undriven_7;
  wire [4:0] undriven_3;
  wire [31:0] multiplexer_1_out, multiplexer_2_out, undriven, undriven_2, undriven_4, undriven_5, undriven_6;

  Add_32_Bit add_32_bit_1 ();
  Set_Less_Than set_less_than_1 ();
  Multiplexer #(.select(5), .width(32), .enable("false")) multiplexer_1 (
    .in0(undriven_4), .in1(undriven), .in30(undriven_5), .in31(undriven_2), .out(multiplexer_1_out),
    .sel(undriven_3));  // open: in2, in3, in4, in5, in6, in7, in8, in9, in10, in11, in12, in13, in14, in15, in16, in17, in18, in19, in20, in21, in22, in23, in24, in25, in26, in27, in28, in29
  Multiplexer #(.width(32), .enable("false")) multiplexer_2 (
    .in0(multiplexer_1_out), .in1(undriven_6), .out(multiplexer_2_out), .sel(undriven_7));

  // Notes on the sheet:
  //   X[00]
  //   X[01]
  //   .
  //   .
  //   .
  //   .
  //   X[30]
  //   X[31]
  //   Y[31]
  //   Y[30]
  //   .
  //   .
  //   .
  //   .
  //   Y[01]
  //   Y[00]
  //   I[31]
  //   I30]
  //   .
  //   .
  //   .
  //   .
  //   I[01]
  //   I[00]
  //   1'b0
  //   V
  //   Z
endmodule

module Shift_Right_32_Bit (
);

  wire multiplexer_1_out, undriven, undriven_2, undriven_3;

  Shift_Right_1_Bit shift_right_1_bit_1 ();
  Shift_Right_1_Bit shift_right_1_bit_2 ();
  Multiplexer #(.enable("false")) multiplexer_1 (
    .in0(undriven_2), .in1(undriven), .out(multiplexer_1_out), .sel(undriven_3));

  // Notes on the sheet:
  //   X[00]
  //   X[01]
  //   .
  //   .
  //   .
  //   .
  //   X[30]
  //   X[31]
  //   Y[31]
  //   Y[30]
  //   .
  //   .
  //   .
  //   .
  //   Y[01]
  //   Y[00]
  //   31
  //   30
  //   .
  //   .
  //   .
  //   .
  //   01
  //   00
  //   .
  //   .
  //   32 Bit Bus
  //   32'b0
  //   Z
endmodule

module Shift_Left_32_Bit (
);

  wire multiplexer_1_out, undriven, undriven_2, undriven_3;

  Shift_Left_1_Bit shift_left_1_bit_1 ();
  Shift_Left_1_Bit shift_left_1_bit_2 ();
  Multiplexer #(.enable("false")) multiplexer_1 (
    .in0(undriven_2), .in1(undriven), .out(multiplexer_1_out), .sel(undriven_3));

  // Notes on the sheet:
  //   X[00]
  //   X[01]
  //   .
  //   .
  //   .
  //   .
  //   X[30]
  //   X[31]
  //   Y[31]
  //   Y[30]
  //   .
  //   .
  //   .
  //   .
  //   Y[01]
  //   Y[00]
  //   31
  //   30
  //   .
  //   .
  //   .
  //   .
  //   01
  //   00
  //   .
  //   .
  //   32 Bit Bus
  //   32'b0
  //   Z
endmodule

module Shift_Right_A_32_Bit (
);

  wire multiplexer_2_out, or_1_out, undriven, undriven_2, undriven_3, undriven_4, undriven_5, undriven_6,
       undriven_7;
  wire [1:0] multiplexer_1_out;

  Shift_Right_1_Bit shift_right_1_bit_1 ();
  Shift_Right_1_Bit shift_right_1_bit_2 ();
  Add_32_Bit add_32_bit_1 ();
  Set_Less_Than set_less_than_1 ();
  Set_Less_Than set_less_than_2 ();
  Multiplexer #(.enable("false")) multiplexer_1 (
    .in0(undriven_2), .in1(undriven_3), .out(multiplexer_1_out[0]), .sel(undriven));
  or or_1 (or_1_out, undriven_4, undriven_5);
  Multiplexer #(.select(2), .enable("false")) multiplexer_2 (
    .in0(undriven_6), .in1(undriven_7), .in2(undriven_7), .in3(undriven_7), .out(multiplexer_2_out),
    .sel(multiplexer_1_out));
  // Pins of 1 and 2 bits meet at multiplexer_1_out

  // Notes on the sheet:
  //   X[00]
  //   X[01]
  //   .
  //   .
  //   .
  //   .
  //   X[30]
  //   X[31]
  //   Y[31]
  //   Y[30]
  //   .
  //   .
  //   .
  //   .
  //   Y[01]
  //   Y[00]
  //   31
  //   30
  //   .
  //   .
  //   .
  //   .
  //   01
  //   00
  //   .
  //   .
  //   1'b0
  //   32'd31
  //   32b'1
  //   1'b1
  //   1'b0
  //   32'b0
endmodule

module ALU (
);

  wire and_1_out, multiplexer_1_out, multiplexer_2_out, multiplexer_3_out, multiplexer_4_out,
       multiplexer_5_out, multiplexer_6_out, multiplexer_7_out, multiplexer_8_out, nor_1_out, or_1_out,
       undriven, undriven_2, undriven_3, undriven_4, undriven_5, undriven_6, undriven_7, undriven_8,
       undriven_9, undriven_10, undriven_11, undriven_12, undriven_14, undriven_16, undriven_17, undriven_18,
       undriven_19, xor_1_out, xor_2_out, xor_3_out;
  wire [1:0] undriven_15;
  wire [3:0] undriven_13;

  blank Adder ();
  blank Subtractor ();
  blank Set_Less_Than ();
  blank Shift_Right_Logical ();
  blank Shift_Left_Logical ();
  blank Shift_Right_Arithmetic ();
  and and_1 (and_1_out, undriven, undriven_2);
  or or_1 (or_1_out, undriven, undriven_2);
  xor xor_1 (xor_1_out, undriven, undriven_2);
  nor nor_1 (nor_1_out, undriven, undriven_2);
  blank Equals ();
  blank Equals_2 ();
  xor xor_2 (xor_2_out, undriven, undriven_2);
  xor xor_3 (xor_3_out, undriven, undriven_2);
  blank Equals_3 ();
  blank Equals_4 ();
  Multiplexer #(.select(4), .enable("false")) multiplexer_1 (
    .in0(and_1_out), .in1(or_1_out), .in2(xor_1_out), .in3(nor_1_out), .in4(undriven_4), .in5(undriven_3),
    .in6(undriven_5), .in7(undriven_6), .in8(undriven_7), .in9(undriven_8), .in10(undriven_9),
    .in11(undriven_12), .in12(undriven_12), .in13(undriven_12), .in14(undriven_12), .in15(undriven_12),
    .out(multiplexer_1_out), .sel(undriven_13));
  Multiplexer #(.select(4), .enable("false")) multiplexer_2 (
    .in0(undriven_11), .in1(undriven_11), .in2(undriven_11), .in3(undriven_11), .in4(undriven_11),
    .in5(undriven_11), .in6(undriven_11), .in7(undriven_11), .in8(undriven_11), .in9(undriven_10),
    .in10(undriven_10), .in11(undriven_10), .in12(undriven_10), .in13(undriven_10), .in14(undriven_10),
    .in15(undriven_10), .out(multiplexer_2_out), .sel(undriven_13));
  Multiplexer #(.enable("false")) multiplexer_3 (
    .in0(undriven_14), .in1(xor_2_out), .out(multiplexer_3_out), .sel(xor_2_out));
  Multiplexer #(.enable("false")) multiplexer_4 (
    .in0(xor_3_out), .in1(undriven_14), .out(multiplexer_4_out), .sel(xor_3_out));
  Multiplexer #(.enable("false")) multiplexer_5 (
    .in0(undriven_19), .in1(undriven_16), .out(multiplexer_5_out), .sel(multiplexer_2_out));
  Multiplexer #(.enable("false")) multiplexer_6 (
    .in0(undriven_19), .in1(undriven_17), .out(multiplexer_6_out), .sel(multiplexer_2_out));
  Multiplexer #(.select(2), .enable("false")) multiplexer_7 (
    .in0(undriven_18), .in1(multiplexer_3_out), .in2(multiplexer_4_out), .in3(undriven_18),
    .out(multiplexer_7_out), .sel(undriven_15));
  Multiplexer #(.enable("false")) multiplexer_8 (
    .in0(undriven_18), .in1(multiplexer_7_out), .out(multiplexer_8_out), .sel(multiplexer_2_out));

  // Notes on the sheet:
  //   X[00]
  //   X[01]
  //   .
  //   .
  //   .
  //   .
  //   X[30]
  //   X[31]
  //   32'b0
  //   Y[31]
  //   Y[30]
  //   .
  //   .
  //   .
  //   .
  //   Y[01]
  //   Y[00]
  //   op_code
  //   X
  //   Y
  //   Cin
  //   X
  //   Y
  //   Cin
  //   X
  //   Y
  //   X
  //   Y
  //   X
  //   Y
  //   X
  //   Y
  //   32'b0
  //   Z
  //   Cout
  //   Z
  //   Cout
  //   Z
  //   Z
  //   Z
  //   Z
  //   4'b0101
  //   4'b0110
  //   X
  //   Y
  //   X
  //   Y
  //   32'b0
  //   32'b0
  //   32'b1
  //   32'b0
  //   Z
  //   Z
  //   32'b0
  //   X
  //   Y
  //   X
  //   Y
  //   32'b0
  //   Z
  //   Z
  //   1'b0
  //   is_valid
  //   Equal
  //   Zero
  //   Z
  //   Overflow
endmodule
