// Logisim project add_32bit.circ as structural Verilog: 1 circuit, main circuit main
module main (
);

  wire adder_1_cout, adder_1_out, adder_2_cout, adder_2_out, adder_3_cout, adder_3_out, adder_4_cout,
       adder_4_out, undriven, undriven_2, undriven_3, undriven_4, undriven_5, undriven_6, undriven_7,
       undriven_8, undriven_9, undriven_10;

  Adder #(.width(1)) adder_1 (.a(undriven), .b(undriven_9), .out(adder_1_out), .cin(adder_2_cout), .cout(adder_1_cout));
  Adder #(.width(1)) adder_2 (
    .a(undriven_2), .b(undriven_5), .out(adder_2_out), .cin(undriven_10), .cout(adder_2_cout));
  Adder #(.width(1)) adder_3 (
    .a(undriven_3), .b(undriven_6), .out(adder_3_out), .cin(adder_4_cout), .cout(adder_3_cout));
  Adder #(.width(1)) adder_4 (.a(undriven_4), .b(undriven_7), .out(adder_4_out), .cin(undriven_8), .cout(adder_4_cout));

  // Notes on the sheet:
  //   X[31]
  //   X[30]
  //   .
  //   .
  //   .
  //   .
  //   X[01]
  //   X[00]
  //   Y[31]
  //   Y[30]
  //   .
  //   .
  //   .
  //   .
  //   Y[01]
  //   Y[00]
  //   C_IN
  //   32 Bit Ripple Adder
  //   .
  //   .
  //   .
  //   .
  //   C_OUT
  //   Z[31]
  //   Z[30]
  //   .
  //   .
  //   .
  //   .
  //   Z[01]
  //   Z[00]
endmodule
