// Logisim project sub_1bit.circ as structural Verilog: 1 circuit, main circuit main
module main (
);

  wire and_1_out, multiplexer_1_out, or_1_out, undriven, undriven_2, undriven_3, xor_1_out, xor_2_out;

  xor xor_1 (xor_1_out, undriven_3, undriven);
  or or_1 (or_1_out, undriven, undriven_2);
  and and_1 (and_1_out, undriven, undriven_2);
  xor xor_2 (xor_2_out, xor_1_out, undriven_2);
  Multiplexer #(.enable("false")) multiplexer_1 (
    .in0(or_1_out), .in1(and_1_out), .out(multiplexer_1_out), .sel(undriven_3));

  // Notes on the sheet:
  //   X
  //   Y
  //   C_IN
  //   1 Bit Subtracter
  //   Z
  //   C_OUT
endmodule
