// Logisim project sub_32bit.circ as structural Verilog: 1 circuit, main circuit main
module main (
);

  wire subtractor_1_bout, subtractor_2_bout, subtractor_3_bout, subtractor_4_bout, undriven_6, undriven_10;
  wire [7:0] subtractor_1_out, subtractor_2_out, subtractor_3_out, subtractor_4_out, undriven, undriven_2,
       undriven_3, undriven_4, undriven_5, undriven_7, undriven_8, undriven_9;

  Subtractor subtractor_1 (
    .a(undriven_8), .b(undriven_3), .out(subtractor_1_out), .bin(undriven_6), .bout(subtractor_1_bout));
  Subtractor subtractor_2 (
    .a(undriven_2), .b(undriven_9), .out(subtractor_2_out), .bin(subtractor_1_bout), .bout(subtractor_2_bout));
  Subtractor subtractor_3 (
    .a(undriven), .b(undriven_5), .out(subtractor_3_out), .bin(undriven_10), .bout(subtractor_3_bout));
  Subtractor subtractor_4 (
    .a(undriven_7), .b(undriven_4), .out(subtractor_4_out), .bin(subtractor_3_bout), .bout(subtractor_4_bout));

  // Notes on the sheet:
  //   X[31]
  //   X[30]
  //   .
  //   .
  //   .
  //   .
  //   X[01]
  //   X[00]
  //   Y[31]
  //   Y[30]
  //   .
  //   .
  //   .
  //   .
  //   Y[01]
  //   Y[00]
  //   C_IN
  //   32 Bit Ripple Subtractor
  //   .
  //   .
  //   .
  //   .
  //   C_OUT
  //   Z[31]
  //   Z[30]
  //   .
  //   .
  //   .
  //   .
  //   Z[01]
  //   Z[00]
endmodule
